// Logisim project Calculator.circ as structural Verilog: 7 circuits, main circuit calculator
module calculator (
  input  [3:0] in_1
);

  wire sevsegcontroller_1_seg_1, sevsegcontroller_1_seg_2, sevsegcontroller_1_seg_3,
       sevsegcontroller_1_seg_4, sevsegcontroller_1_seg_5, sevsegcontroller_1_seg_6,
       sevsegcontroller_1_seg_7, sevsegcontroller_1_seg_8, sevsegcontroller_2_seg_1,
       sevsegcontroller_2_seg_2, sevsegcontroller_2_seg_3, sevsegcontroller_2_seg_4,
       sevsegcontroller_2_seg_5, sevsegcontroller_2_seg_6, sevsegcontroller_2_seg_7,
       sevsegcontroller_2_seg_8, sevsegcontroller_3_seg_1, sevsegcontroller_3_seg_2,
       sevsegcontroller_3_seg_3, sevsegcontroller_3_seg_4, sevsegcontroller_3_seg_5,
       sevsegcontroller_3_seg_6, sevsegcontroller_3_seg_7, sevsegcontroller_3_seg_8;

  edgeDetector edgedetector_1 ();  // open: Input, Clk, Edge_Raising, Edge_Falling
  Button p1 ();  // open: out
  edgeDetector edgedetector_2 ();  // open: Input, Clk, Edge_Raising, Edge_Falling
  Button m1 ();  // open: out
  edgeDetector edgedetector_3 ();  // open: Input, Clk, Edge_Raising, Edge_Falling
  Button p10 ();  // open: out
  edgeDetector edgedetector_4 ();  // open: Input, Clk, Edge_Raising, Edge_Falling
  Button m10 ();  // open: out
  edgeDetector edgedetector_5 ();  // open: Input, Clk, Edge_Raising, Edge_Falling
  Button ADD ();  // open: out
  edgeDetector edgedetector_6 ();  // open: Input, Clk, Edge_Raising, Edge_Falling
  Button SUB ();  // open: out
  edgeDetector edgedetector_7 ();  // open: Input, Clk, Edge_Raising, Edge_Falling
  Button MUL ();  // open: out
  edgeDetector edgedetector_8 ();  // open: Input, Clk, Edge_Raising, Edge_Falling
  Button DIV ();  // open: out
  edgeDetector edgedetector_9 ();  // open: Input, Clk, Edge_Raising, Edge_Falling
  Button Enter ();  // open: out
  edgeDetector edgedetector_10 ();  // open: Input, Clk, Edge_Raising, Edge_Falling
  Button Reset ();  // open: out
  arithmeticLogicUnit arithmeticlogicunit_1 ();  // open: Input2, Input1, Op, Result, WE1, WE2, clk, OE
  smartRegister Input_1 ();  // open: Input, WE, clk, R, OE, out_6
  smartRegister Input_2 ();  // open: Input, WE, clk, R, OE, out_6
  smartRegister Result ();  // open: Input, WE, clk, R, OE, out_6
  sevSegController sevsegcontroller_1 (
    .Input(in_1), .Seg_1(sevsegcontroller_1_seg_1), .Seg_2(sevsegcontroller_1_seg_2),
    .Seg_3(sevsegcontroller_1_seg_3), .Seg_4(sevsegcontroller_1_seg_4), .Seg_5(sevsegcontroller_1_seg_5),
    .Seg_6(sevsegcontroller_1_seg_6), .Seg_7(sevsegcontroller_1_seg_7), .Seg_8(sevsegcontroller_1_seg_8));
  _7_Segment_Display u_7_segment_display_1 (
    .g(sevsegcontroller_2_seg_7), .f(sevsegcontroller_2_seg_6), .a(sevsegcontroller_2_seg_1),
    .b(sevsegcontroller_2_seg_2), .e(sevsegcontroller_2_seg_5), .d(sevsegcontroller_2_seg_4),
    .c(sevsegcontroller_2_seg_3), .dp(sevsegcontroller_2_seg_8));
  _7_Segment_Display u_7_segment_display_2 (
    .g(sevsegcontroller_1_seg_7), .f(sevsegcontroller_1_seg_6), .a(sevsegcontroller_1_seg_1),
    .b(sevsegcontroller_1_seg_2), .e(sevsegcontroller_1_seg_5), .d(sevsegcontroller_1_seg_4),
    .c(sevsegcontroller_1_seg_3), .dp(sevsegcontroller_1_seg_8));
  sevSegController sevsegcontroller_2 (
    .Seg_1(sevsegcontroller_2_seg_1), .Seg_2(sevsegcontroller_2_seg_2), .Seg_3(sevsegcontroller_2_seg_3),
    .Seg_4(sevsegcontroller_2_seg_4), .Seg_5(sevsegcontroller_2_seg_5), .Seg_6(sevsegcontroller_2_seg_6),
    .Seg_7(sevsegcontroller_2_seg_7), .Seg_8(sevsegcontroller_2_seg_8));  // open: Input
  sevSegController sevsegcontroller_3 (
    .Seg_1(sevsegcontroller_3_seg_1), .Seg_2(sevsegcontroller_3_seg_2), .Seg_3(sevsegcontroller_3_seg_3),
    .Seg_4(sevsegcontroller_3_seg_4), .Seg_5(sevsegcontroller_3_seg_5), .Seg_6(sevsegcontroller_3_seg_6),
    .Seg_7(sevsegcontroller_3_seg_7), .Seg_8(sevsegcontroller_3_seg_8));  // open: Input
  _7_Segment_Display u_7_segment_display_3 (
    .g(sevsegcontroller_3_seg_7), .f(sevsegcontroller_3_seg_6), .a(sevsegcontroller_3_seg_1),
    .b(sevsegcontroller_3_seg_2), .e(sevsegcontroller_3_seg_5), .d(sevsegcontroller_3_seg_4),
    .c(sevsegcontroller_3_seg_3), .dp(sevsegcontroller_3_seg_8));
  DotMatrix #(.matrixcols(8), .matrixrows(8)) dotmatrix_1 ();  // open: col0, col1, col2, col3, col4, col5, col6, col7
endmodule

module edgeDetector (
  input  Input,
  input  Clk,
  output Edge_Raising,
  output Edge_Falling
);

  wire d_ff_1_q, d_ff_2_q, not_1_out, not_2_out;

  D_Flip_Flop d_ff_1 (.D(Input), .clk(Clk), .Q(d_ff_1_q));  // open: Qn, preset, reset
  D_Flip_Flop d_ff_2 (.D(d_ff_1_q), .clk(Clk), .Q(d_ff_2_q));  // open: Qn, preset, reset
  not not_1 (not_1_out, d_ff_2_q);
  not not_2 (not_2_out, d_ff_1_q);
  and and_1 (Edge_Raising, d_ff_1_q, not_1_out);
  and and_2 (Edge_Falling, d_ff_2_q, not_2_out);
endmodule

module sevSegController (
  input  [3:0] Input,
  output Seg_1,
  output Seg_2,
  output Seg_3,
  output Seg_4,
  output Seg_5,
  output Seg_6,
  output Seg_7,
  output Seg_8
);

  wire and_1_out, and_2_out, and_3_out, and_4_out, and_5_out, and_6_out, and_7_out, and_8_out, and_9_out,
       and_10_out, and_11_out, and_12_out, and_13_out, and_14_out, and_15_out, and_16_out, and_17_out,
       and_18_out, and_19_out, and_20_out, and_21_out, and_22_out, and_23_out, and_24_out, and_25_out,
       not_1_out, not_2_out, not_3_out, not_4_out, not_5_out, not_6_out, not_7_out, not_8_out, not_9_out,
       not_10_out, not_11_out, not_12_out, not_13_out, not_14_out, not_15_out, not_16_out, not_17_out,
       not_18_out, not_19_out, not_20_out, not_21_out, not_22_out, not_23_out, not_24_out, not_25_out,
       not_26_out, not_27_out, not_28_out, not_29_out, not_30_out, not_31_out;

  not not_1 (not_1_out, Input[2]);
  not not_2 (not_2_out, Input[0]);
  not not_3 (not_3_out, Input[3]);
  not not_4 (not_4_out, Input[2]);
  not not_5 (not_5_out, Input[1]);
  not not_6 (not_6_out, Input[0]);
  not not_7 (not_7_out, Input[3]);
  not not_8 (not_8_out, Input[1]);
  not not_9 (not_9_out, Input[0]);
  not not_10 (not_10_out, Input[3]);
  not not_11 (not_11_out, Input[3]);
  not not_12 (not_12_out, Input[2]);
  not not_13 (not_13_out, Input[2]);
  not not_14 (not_14_out, Input[0]);
  not not_15 (not_15_out, Input[3]);
  not not_16 (not_16_out, Input[0]);
  not not_17 (not_17_out, Input[2]);
  not not_18 (not_18_out, Input[1]);
  not not_19 (not_19_out, Input[2]);
  not not_20 (not_20_out, Input[0]);
  not not_21 (not_21_out, Input[3]);
  not not_22 (not_22_out, Input[0]);
  not not_23 (not_23_out, Input[1]);
  not not_24 (not_24_out, Input[0]);
  not not_25 (not_25_out, Input[3]);
  not not_26 (not_26_out, Input[0]);
  not not_27 (not_27_out, Input[1]);
  not not_28 (not_28_out, Input[2]);
  not not_29 (not_29_out, Input[0]);
  not not_30 (not_30_out, Input[1]);
  and and_1 (and_1_out, not_1_out, not_2_out);
  and and_2 (and_2_out, not_3_out, Input[1]);
  and and_3 (and_3_out, Input[2], Input[0]);
  and and_4 (and_4_out, Input[3], not_4_out);
  not not_31 (not_31_out, Input[2]);
  and and_5 (and_5_out, not_5_out, not_6_out);
  and and_6 (and_6_out, not_7_out, Input[1], Input[0]);
  and and_7 (and_7_out, not_8_out, not_9_out);
  and and_8 (and_8_out, not_10_out, Input[0]);
  and and_9 (and_9_out, not_11_out, Input[2]);
  and and_10 (and_10_out, Input[3], not_12_out);
  and and_11 (and_11_out, not_13_out, not_14_out);
  and and_12 (and_12_out, not_15_out, Input[1], not_16_out);
  and and_13 (and_13_out, not_17_out, Input[1]);
  and and_14 (and_14_out, Input[2], not_18_out, Input[0]);
  and and_15 (and_15_out, Input[3], Input[0]);
  and and_16 (and_16_out, not_19_out, not_20_out);
  and and_17 (and_17_out, not_21_out, Input[1], not_22_out);
  and and_18 (and_18_out, Input[3], Input[2], Input[0]);
  and and_19 (and_19_out, not_23_out, not_24_out);
  and and_20 (and_20_out, not_25_out, Input[2], not_26_out);
  and and_21 (and_21_out, Input[2], not_27_out);
  and and_22 (and_22_out, Input[3], Input[0]);
  and and_23 (and_23_out, not_28_out, Input[1]);
  and and_24 (and_24_out, Input[1], not_29_out);
  and and_25 (and_25_out, Input[2], not_30_out);
  or or_1 (Seg_1, and_1_out, and_2_out, and_3_out, and_4_out);
  or or_2 (Seg_2, not_31_out, and_5_out, and_6_out);
  or or_3 (Seg_3, and_7_out, and_8_out, and_9_out, and_10_out);
  or or_4 (Seg_4, and_11_out, and_12_out, and_13_out, and_14_out, and_15_out);
  or or_5 (Seg_5, and_16_out, and_17_out, and_18_out);
  or or_6 (Seg_6, and_19_out, and_20_out, and_21_out, and_22_out);
  or or_7 (Seg_7, and_23_out, and_24_out, and_25_out, Input[3]);

  assign Seg_8 = 1'b0;
endmodule

module arithmeticLogicUnit (
  input  [7:0] Input2,
  input  WE1,
  input  [7:0] Input1,
  input  WE2,
  input  clk,
  input  [1:0] Op,
  input  OE,
  output [7:0] Result
);

  wire [7:0] adder_1_out, divider_1_out, multiplier_1_out, register_1_q, register_2_q, subtractor_1_out;

  Register register_1 (.D(Input2), .en(WE1), .clk(clk), .Q(register_1_q));  // open: clr
  Register register_2 (.D(Input1), .en(WE2), .clk(clk), .Q(register_2_q));  // open: clr
  Adder adder_1 (.a(register_2_q), .b(register_1_q), .out(adder_1_out));  // open: cin, cout
  Subtractor subtractor_1 (.a(register_2_q), .b(register_1_q), .out(subtractor_1_out));  // open: bin, bout
  Multiplier multiplier_1 (.a(register_2_q), .b(register_1_q), .out(multiplier_1_out));  // open: cin, cout
  Divider divider_1 (.a(register_2_q), .b(register_1_q), .out(divider_1_out));  // open: upper, rem
  Multiplexer #(.select(2), .width(8)) multiplexer_1 (
    .in0(adder_1_out), .in1(subtractor_1_out), .in2(multiplier_1_out), .in3(divider_1_out), .out(Result),
    .sel(Op), .en(OE));
endmodule

module centralControUnit (
  input  p1,
  input  m1,
  input  p10,
  input  m10,
  input  ADD,
  input  SUB,
  input  MUL,
  input  DIV,
  input  Next,
  input  Back,
  input  Reset,
  input  [7:0] DBus,
  output Input_1_WE,
  output Input_1_RE,
  output Input_2_WE,
  output Input_2_RE,
  output Result_WE,
  output Result_RE,
  output ALU_In1_WE,
  output ALU_In2_WE,
  output ALU_Res_RE
);

  Register StateRegister ();  // open: D, en, Q, clk, clr
endmodule

module smartRegister (
  input  [7:0] Input,
  input  WE,
  input  clk,
  input  R,
  input  OE,
  output [7:0] out_6
);

  wire [7:0] register_1_q;

  Register register_1 (.D(Input), .en(WE), .clk(clk), .Q(register_1_q), .clr(R));
  Multiplexer #(.width(8)) multiplexer_1 (.in0(register_1_q), .out(out_6), .sel(1'b0), .en(OE));  // open: in1
endmodule

module binaryToDecimal (
  input  b0,
  input  b1,
  input  b2,
  input  b3,
  input  b4,
  input  b5,
  input  b6,
  input  b7,
  output out_9,
  output out_10,
  output out_11,
  output out_12,
  output out_13,
  output out_14,
  output out_15,
  output out_16,
  output out_17,
  output out_18,
  output out_19,
  output out_20
);
endmodule
